# Fritzing sketch circuit (saved by Fritzing 0.9.3b)
breadboards: 1

parts:
  부품1 = Arduino Uno (Rev3)
  J1 = Basic Servo
  hc-sr1 = hc-sr04
  Mod1 = sensor_biometrico

nets:
  N1: 부품1.D9_PWM, J1.pulse
  N2: 부품1.D12/MISO, hc-sr1.Trig
  N3: 부품1.D2, Mod1.RX
  N4: 부품1.D3_PWM, Mod1.TX
  VCC: 부품1.5V, J1.vcc, hc-sr1.VCC, Mod1.VCC
  GND: 부품1.GND, J1.gnd, hc-sr1.GND, Mod1.GND

custom parts:
  sensor_biometrico: Adafruit Optical Fingerprint Sensor
