# Fritzing sketch 30 (saved by Fritzing 0.9.3b)
breadboards: 1

parts:
  R1 = Resistor [tolerance=±5% resistance=220 package=THT]
  LED1 = LED - 5mm [color="Green (555nm)" package="5 mm [THT]"]
  J1 = Piezo Speaker
  부품1 = Arduino Uno (Rev3)
  VCC1 = Battery  # not connected
  hc-sr1 = hc-sr04
  부품3 = MQ-4
  R2 = Resistor [tolerance=±5% resistance=220 package=THT]
  R3 = Resistor [tolerance=±5% resistance=220 package=THT]
  LED2 = LED - 5mm [color="Yellow (592nm)" package="5 mm [THT]"]
  LED3 = LED - 5mm [color="Red (633nm)" package="5 mm [THT]"]
  hc-sr2 = hc-sr04
  BT1 = Bluetooth HC-06u [package=THT]
  S1 = SPST Switch [package=switch-spdt-smd]  # not connected

nets:
  GND: R1.Pin_0, J1.pin1, 부품1.GND, hc-sr1.GND, 부품3.GND, R2.Pin_0, R3.Pin_0, hc-sr2.GND, BT1.GND
  N1: R1.Pin_1, LED1.cathode
  N2: LED1.anode, 부품1.D7
  N3: J1.pin2, 부품1.D12/MISO
  N4: 부품1.A0, 부품3.AO
  N5: 부품1.D8, hc-sr1.Echo
  N6: 부품1.D9_PWM, hc-sr1.Trig
  N7: 부품1.D10_PWM/SS, hc-sr2.Echo
  N8: 부품1.D11_PWM/MOSI, hc-sr2.Trig
  N9: 부품1.D2, BT1.RXD
  N10: 부품1.D3_PWM, BT1.TXD
  N11: 부품1.D5_PWM, LED3.anode
  N12: 부품1.D6_PWM, LED2.anode
  VCC: 부품1.5V, hc-sr1.VCC, 부품3.VCC, hc-sr2.VCC, BT1.VCC
  N13: R2.Pin_1, LED2.cathode
  N14: R3.Pin_1, LED3.cathode

custom parts:
  Bluetooth HC-06u: Bluetooth HC-06 - face up, pins down 16.5mm x 37.5mm PCB
